# Fritzing sketch Circuit Diagram (saved by Fritzing 0.9.10b)
perfboards: 1

parts:
  元件1 = LED Matrix - Serial Interface - Red/Green/Blue
  R1 = Resistor [tolerance=±5% power=0.25 resistance=220 package=THT]  # not connected
  S1 = Pushbutton [package="[THT]"]
  元件18 = ws2812b [package="smd 2812b"]  # not connected
  元件30 = ws2812b [package="smd 2812b"]  # not connected
  元件5 = ws2812b [package="smd 2812b"]  # not connected
  元件8 = ws2812b [package="smd 2812b"]  # not connected
  元件4 = ws2812b [package="smd 2812b"]  # not connected
  元件34 = ws2812b [package="smd 2812b"]
  元件31 = ws2812b [package="smd 2812b"]  # not connected
  元件38 = ws2812b [package="smd 2812b"]  # not connected
  元件27 = ws2812b [package="smd 2812b"]  # not connected
  元件19 = ws2812b [package="smd 2812b"]  # not connected
  元件6 = ws2812b [package="smd 2812b"]  # not connected
  元件9 = ws2812b [package="smd 2812b"]  # not connected
  元件14 = ws2812b [package="smd 2812b"]  # not connected
  元件35 = ws2812b [package="smd 2812b"]  # not connected
  元件32 = ws2812b [package="smd 2812b"]  # not connected
  元件33 = ws2812b [package="smd 2812b"]  # not connected
  元件20 = ws2812b [package="smd 2812b"]  # not connected
  元件24 = ws2812b [package="smd 2812b"]  # not connected
  元件36 = ws2812b [package="smd 2812b"]  # not connected
  元件22 = ws2812b [package="smd 2812b"]  # not connected
  元件3 = ws2812b [package="smd 2812b"]  # not connected
  元件12 = ws2812b [package="smd 2812b"]  # not connected
  元件26 = ws2812b [package="smd 2812b"]  # not connected
  元件29 = ws2812b [package="smd 2812b"]  # not connected
  元件25 = ws2812b [package="smd 2812b"]  # not connected
  元件37 = ws2812b [package="smd 2812b"]  # not connected
  元件11 = ws2812b [package="smd 2812b"]  # not connected
  元件10 = ws2812b [package="smd 2812b"]  # not connected
  元件15 = ws2812b [package="smd 2812b"]  # not connected
  元件28 = ws2812b [package="smd 2812b"]  # not connected
  元件17 = ws2812b [package="smd 2812b"]  # not connected
  元件21 = ws2812b [package="smd 2812b"]  # not connected
  元件13 = ws2812b [package="smd 2812b"]  # not connected
  元件23 = ws2812b [package="smd 2812b"]  # not connected
  元件7 = ws2812b [package="smd 2812b"]  # not connected
  元件16 = ws2812b [package="smd 2812b"]  # not connected
  Part1 = Arduino MKR1000
  J1 = Basic Servo

nets:
  VDD: 元件1.SCK, 元件34.VDD, Part1.5V, J1.vcc
  N1: 元件1.CS, Part1.D11_SDA
  N2: 元件1.MISO, Part1.D12_SCL
  GND: 元件1.GND, 元件34.DIN, J1.gnd
  N3: S1.Pin_1, S1.Pin_2
  N4: S1.Pin_3, S1.Pin_4

custom parts:
  Arduino MKR1000: MKR1000 is a powerful board that combines the functionality of the Zero and the Wi-Fi Shield. It is the ideal solution for makers wanting to design IoT projects with minimal previous experience in networking
